// Logisim project 19BCE0215_Q4part1.circ as structural Verilog: 1 circuit, main circuit main
module main (
  input  in_1,
  input  [2:0] in_2,
  input  in_3,
  input  [2:0] in_4,
  output SUM,
  output CARRY,
  output DIFFERENCE,
  output BORROW
);

  wire decoder_1_out0, decoder_1_out1, decoder_1_out2, decoder_1_out3, decoder_1_out4, decoder_1_out5,
       decoder_1_out6, decoder_1_out7, decoder_2_out0, decoder_2_out1, decoder_2_out2, decoder_2_out3,
       decoder_2_out4, decoder_2_out7;

  Decoder #(.select(3)) decoder_1 (
    .out0(decoder_1_out0), .out1(decoder_1_out1), .out2(decoder_1_out2), .out3(decoder_1_out3),
    .out4(decoder_1_out4), .out5(decoder_1_out5), .out6(decoder_1_out6), .out7(decoder_1_out7), .sel(in_2),
    .en(in_1));
  Decoder #(.select(3)) decoder_2 (
    .out0(decoder_2_out0), .out1(decoder_2_out1), .out2(decoder_2_out2), .out3(decoder_2_out3),
    .out4(decoder_2_out4), .out7(decoder_2_out7), .sel(in_4), .en(in_3));  // open: out5, out6
  or or_1 (SUM, decoder_1_out1, decoder_1_out2, decoder_1_out4, decoder_1_out7);
  or or_2 (CARRY, decoder_1_out3, decoder_1_out5, decoder_1_out6, decoder_1_out7);
  or or_3 (DIFFERENCE, decoder_2_out1, decoder_2_out2, decoder_2_out4, decoder_2_out7);
  or or_4 (BORROW, decoder_2_out3, decoder_2_out1, decoder_2_out2, decoder_2_out7);

  // Notes on the sheet:
  //   FULL ADDER
  //   FULL SUBTRACTOR
  //   VIBHU KUMAR SINGH
  //   19BCE0215
  //   VIBHU KUMAR SINGH
  //   19BCE0215
endmodule
