// Logisim project 19BCE0215_Q4part2.circ as structural Verilog: 1 circuit, main circuit main
module main (
  input  in_1,
  input  [1:0] in_2,
  input  in_3,
  input  in_4
);

  wire clock_1_out, d_ff_1_q, d_ff_2_q, d_ff_3_q, multiplexer_1_out;

  Multiplexer #(.select(2)) multiplexer_1 (
    .in0(d_ff_1_q), .in1(in_1), .in2(d_ff_2_q), .in3(d_ff_3_q), .out(multiplexer_1_out), .sel(in_2), .en(in_3));
  Clock clock_1 (.out(clock_1_out));
  D_Flip_Flop d_ff_1 (.clk(clock_1_out), .Q(d_ff_1_q), .en(in_4));  // open: D, Qn, preset, reset
  D_Flip_Flop d_ff_2 (.clk(clock_1_out), .Q(d_ff_2_q), .en(in_4));  // open: D, Qn, preset, reset
  D_Flip_Flop d_ff_3 (.clk(clock_1_out), .D(multiplexer_1_out), .Q(d_ff_3_q), .en(in_4));  // open: Qn, preset, reset

  // Notes on the sheet:
  //   Di
  //   VIBHU KUMAR SINGH
  //   19BCE0215
endmodule
