// Logisim project 19BCE0215_EXP_1.5(Word_Problems).circ as structural Verilog: 1 circuit, main circuit main
module main (
  input  A,
  input  A_2,
  input  B,
  input  B_2,
  input  C,
  input  C_2,
  input  D,
  input  A_3,
  input  A_4,
  input  B_3,
  input  B_4,
  input  C_3,
  input  C_4,
  input  D_2,
  input  D_3,
  input  A_5,
  input  B_5,
  input  C_5,
  input  D_4,
  output out_20,
  output out_21,
  output out_22,
  output out_23,
  output out_24
);

  wire and_1_out, and_2_out, and_3_out, and_4_out, and_5_out, and_6_out, and_7_out, and_8_out, and_9_out,
       nand_1_out, nand_2_out, not_1_out, not_2_out;

  not not_1 (not_1_out, C_5);
  not not_2 (not_2_out, D_4);
  and and_1 (and_1_out, A_2, B_2);
  and and_2 (and_2_out, A_3, C_3, D_2);
  and and_3 (and_3_out, B_3, C_3, D_2);
  or or_1 (out_20, and_1_out, C_2);
  or or_2 (out_22, and_2_out, and_3_out);
  and and_4 (and_4_out, A_5, B_5, not_1_out);
  and and_5 (and_5_out, A_5, B_5, not_2_out);
  and and_6 (and_6_out, A_5, not_1_out, not_2_out);
  and and_7 (and_7_out, B_5, not_1_out, not_2_out);
  or or_3 (out_24, and_4_out, and_5_out, and_6_out, and_7_out);
  and and_8 (and_8_out, A, B, C);
  and and_9 (and_9_out, C, D);
  nand nand_1 (nand_1_out, A_4, C_4, D_3);
  nand nand_2 (nand_2_out, B_4, C_4, D_3);
  nand nand_3 (out_23, nand_1_out, nand_2_out);
  or or_4 (out_21, and_8_out, and_9_out);

  // Notes on the sheet:
  //   F=(A.B+C)
  //   F=(A.C.D)+(B.C.D)
  //   F=(A.B.C')+(A.B.D')+(A.C'.D')+(B.C'.D')
  //   VIBHU KUMAR SINGH
  //   19BCE0215
  //   VIBHU KUMAR SINGH
  //   19BCE0215
  //   VIBHU KUMAR SINGH
  //   19BCE0215
  //   F=(A.B.C+C.D)
  //   F=(A+B).C.D
  //   VIBHU KUMAR SINGH
  //   19BCE0215
  //   VIBHU KUMAR SINGH
  //   19BCE0215
endmodule
