// Logisim project Basic_gates_using_universal_gates.circ as structural Verilog: 1 circuit, main circuit main
module main (
  input  A,
  input  B,
  input  A_2,
  input  B_2,
  output NOT,
  output AND,
  output OR,
  output NOT_2,
  output AND_2,
  output OR_2
);

  wire nand_2_out, nand_3_out, nand_4_out, nor_2_out, nor_3_out, nor_4_out;

  nand nand_1 (NOT, A, A);
  nand nand_2 (nand_2_out, A, B);
  nand nand_3 (nand_3_out, A, A);
  nand nand_4 (nand_4_out, B, B);
  nor nor_1 (NOT_2, A_2, A_2);
  nor nor_2 (nor_2_out, A_2, A_2);
  nor nor_3 (nor_3_out, B_2, B_2);
  nor nor_4 (nor_4_out, A_2, B_2);
  nand nand_5 (AND, nand_2_out, nand_2_out);
  nand nand_6 (OR, nand_3_out, nand_4_out);
  nor nor_5 (AND_2, nor_2_out, nor_3_out);
  nor nor_6 (OR_2, nor_4_out, nor_4_out);

  // Notes on the sheet:
  //   VIBHU KUMAR SINGH
  //   19BCE0215
  //   VIBHU KUMAR SINGH
  //   19BCE0215
endmodule
