// Logisim project Verification_of_DeMorgans.circ as structural Verilog: 1 circuit, main circuit main
module main (
  input  A,
  input  B,
  input  C,
  input  A_2,
  input  B_2,
  input  C_2,
  input  A_3,
  input  B_3,
  input  C_3,
  input  A_4,
  input  B_4,
  input  C_4,
  output out_13,
  output out_14,
  output out_15,
  output out_16
);

  wire and_1_out, not_1_out, not_2_out, not_3_out, not_4_out, not_5_out, not_6_out, or_1_out;

  not not_1 (not_1_out, A_2);
  not not_2 (not_2_out, B_2);
  not not_3 (not_3_out, C_2);
  not not_4 (not_4_out, A_4);
  not not_5 (not_5_out, B_4);
  not not_6 (not_6_out, C_4);
  and and_1 (and_1_out, A, B, C);
  or or_1 (or_1_out, A_3, B_3, C_3);
  not not_7 (out_13, and_1_out);
  or or_2 (out_14, not_1_out, not_2_out, not_3_out);
  not not_8 (out_15, or_1_out);
  and and_2 (out_16, not_4_out, not_5_out, not_6_out);

  // Notes on the sheet:
  //   (A.B.C)'=(A'+B'+C')
  //   VIBHU KUMAR SINGH
  //   19BCE0215
  //   (A+B+C)'=(A'.B'.C')
  //   VIBHU KUMAR SINGH
  //   19BCE0215
endmodule
