// Logisim project 7Segmentdisplay.circ as structural Verilog: 1 circuit, main circuit main
module main (
  input  X,
  input  Y
);

  wire not_1_out, not_2_out, or_1_out, or_2_out, or_3_out;

  not not_1 (not_1_out, X);
  not not_2 (not_2_out, Y);
  or or_1 (or_1_out, X, not_2_out);
  or or_2 (or_2_out, Y, not_1_out);
  or or_3 (or_3_out, X, Y);
  _7_Segment_Display u_7_segment_display_1 (
    .g(or_3_out), .f(or_1_out), .a(1'b1), .b(or_2_out), .e(not_2_out), .d(1'b1), .c(1'b1));  // open: dp

  // Notes on the sheet:
  //   19BCE0215
  //   VIBHU KUMAR SINGH
endmodule
