// Logisim project ADDERS.circ as structural Verilog: 1 circuit, main circuit main
module main (
  input  X,
  input  X_2,
  input  Y,
  input  Y_2,
  input  Z,
  input  X_3,
  input  Y_3,
  input  X_4,
  input  Z_2,
  input  Y_4,
  input  Z_3,
  output SUM,
  output SUM_2,
  output CARRY,
  output CARRY_2,
  output SUM_3,
  output SUM_4,
  output CARRY_3,
  output CARRY_4
);

  wire adder_1_cout, adder_1_out, adder_2_cout, and_1_out, and_2_out, and_3_out, and_5_out, and_6_out,
       xor_2_out, xor_4_out;

  xor xor_1 (SUM, X_2, Y_2);
  xor xor_2 (xor_2_out, X_3, Y_3);
  and and_1 (and_1_out, Z_2, X_3);
  and and_2 (and_2_out, X_3, Y_3);
  and and_3 (and_3_out, Y_3, Z_2);
  and and_4 (CARRY, Y_2, X_2);
  xor xor_3 (SUM_3, xor_2_out, Z_2);
  or or_1 (CARRY_4, and_1_out, and_2_out, and_3_out);
  xor xor_4 (xor_4_out, X, Y);
  and and_5 (and_5_out, X, Y);
  Adder #(.width(1)) adder_1 (.a(X_4), .b(Y_4), .out(adder_1_out), .cout(adder_1_cout));  // open: cin
  and and_6 (and_6_out, xor_4_out, Z);
  xor xor_5 (SUM_2, xor_4_out, Z);
  or or_2 (CARRY_2, and_6_out, and_5_out);
  Adder #(.width(1)) adder_2 (.a(adder_1_out), .b(Z_3), .out(SUM_4), .cout(adder_2_cout));  // open: cin
  or or_3 (CARRY_3, adder_2_cout, adder_1_cout);

  // Notes on the sheet:
  //   HALF ADDER
  //   FULL ADDER
  //   VIBHU KUMAR SINGH
  //   19BCE0215
  //   VIBHU KUMAR SINGH
  //   19BCE0215
  //   FULL ADDER USING HALF ADDERS
  //   VIBHU KUMAR SINGH
  //   19BCE0215
  //   FULL ADDER USING IC
  //   VIBHU KUMAR SINGH
  //   19BCE0215
endmodule
