// Logisim project CODE_CONVERTERS.circ as structural Verilog: 1 circuit, main circuit main
module main (
  input  A,
  input  B,
  input  C,
  input  D,
  input  A_2,
  input  B_2,
  input  C_2,
  input  D_2,
  output W,
  output X,
  output Y,
  output Z,
  output W_2,
  output X_2,
  output Y_2,
  output Z_2
);

  wire and_1_out, and_2_out, and_3_out, and_4_out, and_5_out, and_6_out, and_7_out, and_8_out, and_9_out,
       not_1_out, not_2_out, not_3_out, xor_1_out, xor_2_out, xor_3_out;

  not not_1 (not_1_out, A);
  and and_1 (and_1_out, B, C, D);
  and and_2 (and_2_out, not_1_out, B);
  and and_3 (and_3_out, not_1_out, C);
  and and_4 (and_4_out, not_1_out, D);
  xor xor_1 (xor_1_out, C, D);
  or or_1 (X, and_2_out, and_3_out, and_4_out, and_1_out);
  not not_2 (not_2_out, B);
  xor xor_2 (xor_2_out, A, xor_1_out);
  and and_5 (and_5_out, A, not_2_out);
  or or_2 (Y, xor_2_out, and_5_out);
  and and_6 (and_6_out, D_2, C_2, B_2);
  not not_3 (not_3_out, A_2);
  xor xor_3 (xor_3_out, B_2, C_2);
  and and_7 (and_7_out, not_3_out, C_2);
  and and_8 (and_8_out, not_3_out, D_2);
  xor xor_4 (Y_2, xor_3_out, D_2);
  and and_9 (and_9_out, not_3_out, B_2);
  or or_3 (X_2, and_6_out, and_7_out, and_8_out, and_9_out);

  assign W = A;
  assign W_2 = A_2;
  assign Z = D;
  assign Z_2 = D_2;

  // Notes on the sheet:
  //   2 4 2 1 code to 8 4 -2 -1 code
  //   VIBHU KUMAR SINGH
  //   19BCE0215
endmodule
