// Logisim project SUBTRACTORS.circ as structural Verilog: 1 circuit, main circuit main
module main (
  input  X,
  input  X_2,
  input  Y,
  input  Y_2,
  input  Z,
  input  X_3,
  input  X_4,
  input  Y_3,
  input  Y_4,
  input  Z_2,
  input  Z_3,
  output DIFFERENCE,
  output DIFFERENCE_2,
  output BORROW,
  output BORROW_2,
  output DIFFERENCE_3,
  output DIFFERENCE_4,
  output BORROW_3,
  output BORROW_4
);

  wire and_1_out, and_2_out, and_3_out, and_5_out, and_6_out, not_1_out, not_2_out, not_3_out, not_4_out,
       subtractor_1_bout, subtractor_1_out, subtractor_2_bout, xor_2_out, xor_4_out;

  not not_1 (not_1_out, X_2);
  not not_2 (not_2_out, X_3);
  xor xor_1 (DIFFERENCE, X_2, Y_2);
  and and_1 (and_1_out, Z_2, not_2_out);
  and and_2 (and_2_out, not_2_out, Y_3);
  and and_3 (and_3_out, Y_3, Z_2);
  and and_4 (BORROW, Y_2, not_1_out);
  xor xor_2 (xor_2_out, X_3, Y_3);
  xor xor_3 (DIFFERENCE_4, xor_2_out, Z_2);
  or or_1 (BORROW_4, and_1_out, and_2_out, and_3_out);
  not not_3 (not_3_out, X);
  xor xor_4 (xor_4_out, X, Y);
  and and_5 (and_5_out, not_3_out, Y);
  not not_4 (not_4_out, xor_4_out);
  Subtractor #(.width(1)) subtractor_1 (
    .a(X_4), .b(Y_4), .out(subtractor_1_out), .bout(subtractor_1_bout));  // open: bin
  and and_6 (and_6_out, not_4_out, Z);
  xor xor_5 (DIFFERENCE_2, xor_4_out, Z);
  or or_2 (BORROW_2, and_6_out, and_5_out);
  Subtractor #(.width(1)) subtractor_2 (
    .a(subtractor_1_out), .b(Z_3), .out(DIFFERENCE_3), .bout(subtractor_2_bout));  // open: bin
  or or_3 (BORROW_3, subtractor_2_bout, subtractor_1_bout);

  // Notes on the sheet:
  //   HALF SUBTRACTOR
  //   VIBHU KUMAR SINGH
  //   19BCE0215
  //   FULL SUBTRACTOR
  //   VIBHU KUMAR SINGH
  //   19BCE0215
  //   FULL SUBTRACTOR USING HALF SUBTRACTORS
  //   VIBHU KUMAR SINGH
  //   19BCE0215
  //   FULL SUBTRACTOR USING IC
  //   VIBHU KUMAR SINGH
  //   19BCE0215
endmodule
