// Logisim project 2-BIT_MAGNITUDE_COMPARITOR.circ as structural Verilog: 1 circuit, main circuit main
module main (
  input  [1:0] A,
  input  [1:0] B,
  input  [1:0] C,
  output A_B_C,
  output A_is_greatest,
  output B_is_greatest,
  output C_is_greatest
);

  wire comparator_1_eq, comparator_1_gt, comparator_1_lt, comparator_2_eq, comparator_2_gt, comparator_2_lt,
       comparator_3_eq, comparator_3_gt, comparator_3_lt;

  Comparator #(.width(2), .mode("unsigned")) comparator_1 (
    .a(A), .b(B), .gt(comparator_1_gt), .eq(comparator_1_eq), .lt(comparator_1_lt));
  Comparator #(.width(2), .mode("unsigned")) comparator_2 (
    .a(B), .b(C), .gt(comparator_2_gt), .eq(comparator_2_eq), .lt(comparator_2_lt));
  Comparator #(.width(2), .mode("unsigned")) comparator_3 (
    .a(A), .b(C), .gt(comparator_3_gt), .eq(comparator_3_eq), .lt(comparator_3_lt));
  and and_1 (A_B_C, comparator_1_eq, comparator_2_eq, comparator_3_eq);
  and and_2 (A_is_greatest, comparator_1_gt, comparator_3_gt);
  and and_3 (B_is_greatest, comparator_1_lt, comparator_2_gt);
  and and_4 (C_is_greatest, comparator_2_lt, comparator_3_lt);

  // Notes on the sheet:
  //   MAGNITUDE COMPARITOR
  //   VIBHU KUMAR SINGH
  //   19BCE0215
endmodule
