// Logisim project 2X4_DECODER.circ as structural Verilog: 1 circuit, main circuit main
module main (
  input  X,
  input  Y,
  output Do,
  output D1,
  output D2,
  output D3
);

  wire not_1_out, not_2_out;

  not not_1 (not_1_out, Y);
  not not_2 (not_2_out, X);
  and and_1 (Do, not_2_out, not_1_out);
  and and_2 (D1, not_2_out, Y);
  and and_3 (D2, X, not_1_out);
  and and_4 (D3, X, Y);

  // Notes on the sheet:
  //   2X4 DECODER
  //   VIBHU KUMAR SINGH
  //   19BCE0215
endmodule
