// Logisim project 8X4_MUX_USING_2X4_AND_2X1_MUX.circ as structural Verilog: 1 circuit, main circuit main
module main (
  input  Io,
  input  I1,
  input  I2,
  input  I3,
  input  in_5,
  input  I4,
  input  in_7,
  input  I5,
  input  I6,
  input  A,
  input  I7,
  input  [1:0] B_C,
  output out_13
);

  wire multiplexer_1_out, multiplexer_2_out;

  Multiplexer #(.select(2)) multiplexer_1 (
    .in0(Io), .in1(I1), .in2(I2), .in3(I3), .out(multiplexer_1_out), .sel(B_C), .en(in_5));
  Multiplexer #(.select(2)) multiplexer_2 (
    .in0(I4), .in1(I5), .in2(I6), .in3(I7), .out(multiplexer_2_out), .sel(B_C), .en(in_5));
  Multiplexer multiplexer_3 (.in0(multiplexer_1_out), .in1(multiplexer_2_out), .out(out_13), .sel(A), .en(in_7));

  // Notes on the sheet:
  //   8X4 MUX USING 2X4 AND 2X1 MUX
  //   VIBHU KUMAR SINGH
  //   19BCE0215
endmodule
