// Logisim project BINARY_PARALLEL_ADDER.circ as structural Verilog: 1 circuit, main circuit main
module main (
  input  A4,
  input  B4,
  input  A3,
  input  B3,
  input  A2,
  input  B2,
  input  A1,
  input  B1,
  input  Cin,
  output Cout,
  output Sum4,
  output Sum3,
  output Sum2,
  output Sum1
);

  wire main_2_carry, main_3_carry, main_4_carry;

  FULL_ADDER_main main_1 (.X(main_2_carry), .Y(B4), .Z(A4), .SUM(Sum4), .CARRY(Cout));
  FULL_ADDER_main main_2 (.X(main_3_carry), .Y(B3), .Z(A3), .SUM(Sum3), .CARRY(main_2_carry));
  FULL_ADDER_main main_3 (.X(main_4_carry), .Y(B2), .Z(A2), .SUM(Sum2), .CARRY(main_3_carry));
  FULL_ADDER_main main_4 (.X(Cin), .Y(B1), .Z(A1), .SUM(Sum1), .CARRY(main_4_carry));

  // Notes on the sheet:
  //   4-BIT PARALLEL ADDER
  //   VIBHU KUMAR SINGH
  //   19BCE0215
endmodule
