// Logisim project EXCESS_5_TO_BCD_USING_BINARY_PARALLEL_ADDER.circ as structural Verilog: 1 circuit, main circuit main
module main (
  input  A4,
  input  B4,
  input  A3,
  input  B3,
  input  A2,
  input  B2,
  input  A1,
  input  B1,
  input  Cin,
  output Cout,
  output Sum4,
  output Sum1,
  output Sum3,
  output Sum2
);

  BINARY_PARALLEL_ADDER_main main_1 (
    .Cout(Cout), .A4(A4), .B4(B4), .A3(A3), .B3(B3), .A2(A2), .B2(B2), .A1(A1), .B1(B1), .Cin(Cin),
    .Sum4(Sum4), .Sum3(Sum3), .Sum2(Sum2), .Sum1(Sum1));

  // Notes on the sheet:
  //   EXCESS 5 TO BCD USING PARALLEL ADDER
  //   VIBHU KUMAR SINGH
  //   19BCE0215
endmodule
