// Logisim project FULL_ADDER.circ as structural Verilog: 1 circuit, main circuit main
module main (
  input  X,
  input  Y,
  input  Z,
  output SUM,
  output CARRY
);

  wire and_1_out, and_2_out, and_3_out, xor_1_out;

  xor xor_1 (xor_1_out, X, Y);
  and and_1 (and_1_out, Z, X);
  and and_2 (and_2_out, X, Y);
  and and_3 (and_3_out, Y, Z);
  xor xor_2 (SUM, xor_1_out, Z);
  or or_1 (CARRY, and_1_out, and_2_out, and_3_out);

  // Notes on the sheet:
  //   FULL ADDER
  //   19BCE0215
  //   VIBHU KUMAR SINGH
endmodule
