// Logisim project MAGNITUDE_COMPARATOR.circ as structural Verilog: 1 circuit, main circuit main
module main (
  input  [1:0] A,
  input  [1:0] B,
  output A_B,
  output A_B_2,
  output A_B_3
);

  Comparator #(.width(2), .mode("unsigned")) comparator_1 (.a(A), .b(B), .gt(A_B), .eq(A_B_2), .lt(A_B_3));

  // Notes on the sheet:
  //   VIBHU KUMAR SINGH
  //   19BCE0215
  //   2-BIT MAGNITUDE COMPARITOR
endmodule
