// Logisim project PARITY_CHECK.circ as structural Verilog: 1 circuit, main circuit main
module main (
  input  A,
  input  in_2,
  input  [2:0] B_C_D,
  output out_4
);

  wire not_1_out;

  not not_1 (not_1_out, A);
  Multiplexer #(.select(3)) multiplexer_1 (
    .in0(A), .in1(not_1_out), .in2(not_1_out), .in3(A), .in4(not_1_out), .in5(A), .in6(A), .in7(not_1_out),
    .out(out_4), .sel(B_C_D), .en(in_2));

  // Notes on the sheet:
  //   PARITY CHECK
  //   VIBHU KUMAR SINGH
  //   19BCE0215
  //   EVEN PARITY CHECKER
endmodule
