// Logisim project TRAFFIC_LIGHT.circ as structural Verilog: 1 circuit, main circuit main
module main (
  input  in_1,
  input  [3:0] in_2,
  output E_W,
  output N_S
);

  wire decoder_1_out0, decoder_1_out3, decoder_1_out4, decoder_1_out5, decoder_1_out6, decoder_1_out7,
       decoder_1_out8, decoder_1_out9, decoder_1_out10, decoder_1_out11, decoder_1_out13, decoder_1_out14,
       decoder_1_out15;

  Decoder #(.select(4)) decoder_1 (
    .out0(decoder_1_out0), .out3(decoder_1_out3), .out4(decoder_1_out4), .out5(decoder_1_out5),
    .out6(decoder_1_out6), .out7(decoder_1_out7), .out8(decoder_1_out8), .out9(decoder_1_out9),
    .out10(decoder_1_out10), .out11(decoder_1_out11), .out13(decoder_1_out13), .out14(decoder_1_out14),
    .out15(decoder_1_out15), .sel(in_2), .en(in_1));  // open: out1, out2, out12
  or or_1 (E_W, decoder_1_out0, decoder_1_out4, decoder_1_out5, decoder_1_out6, decoder_1_out7, decoder_1_out9, decoder_1_out10, decoder_1_out11, decoder_1_out15);
  or or_2 (N_S, decoder_1_out3, decoder_1_out8, decoder_1_out13, decoder_1_out14);

  // Notes on the sheet:
  //   TRAFFIC LIGHT
  //   VIBHU KUMAR SINGH
  //   19BCE0215
endmodule
