// Logisim project 3BitCounter.circ as structural Verilog: 1 circuit, main circuit main
module main (
  input  in_1,
  input  in_2,
  output A2,
  output A1,
  output A0
);

  wire and_1_out, clock_1_out;

  Clock clock_1 (.out(clock_1_out));
  T_Flip_Flop t_ff_1 (.clk(clock_1_out), .T(and_1_out), .Q(A2), .en(in_2));  // open: Qn, preset, reset
  and and_1 (and_1_out, A1, A0);
  T_Flip_Flop t_ff_2 (.clk(clock_1_out), .Q(A1), .en(in_2));  // open: T, Qn, preset, reset
  T_Flip_Flop t_ff_3 (.clk(clock_1_out), .T(1'b1), .Q(A0), .reset(in_1), .en(in_2));  // open: Qn, preset

  // Notes on the sheet:
  //   clk
  //   VIBHU KUMAR SINGH
  //   19BCE0215
  //   3 Bit Counter
endmodule
