// Logisim project BCDCounter.circ as structural Verilog: 1 circuit, main circuit main
module main (
  input  in_1,
  input  in_2,
  output Q1,
  output Q2,
  output Q4,
  output Q8
);

  wire and_1_out, and_2_out, and_3_out, and_4_out, clock_1_out, or_1_out, t_ff_4_qn;

  Clock clock_1 (.out(clock_1_out));
  T_Flip_Flop t_ff_1 (.clk(clock_1_out), .T(in_1), .Q(Q1), .en(in_2));  // open: Qn, preset, reset
  and and_1 (and_1_out, Q1, t_ff_4_qn);
  T_Flip_Flop t_ff_2 (.clk(clock_1_out), .T(and_1_out), .Q(Q2), .en(in_2));  // open: Qn, preset, reset
  and and_2 (and_2_out, Q2, Q1);
  and and_3 (and_3_out, Q8, Q1);
  and and_4 (and_4_out, and_2_out, Q4);
  T_Flip_Flop t_ff_3 (.clk(clock_1_out), .T(and_2_out), .Q(Q4), .en(in_2));  // open: Qn, preset, reset
  or or_1 (or_1_out, and_4_out, and_3_out);
  T_Flip_Flop t_ff_4 (.clk(clock_1_out), .T(or_1_out), .Q(Q8), .Qn(t_ff_4_qn), .en(in_2));  // open: preset, reset

  // Notes on the sheet:
  //   VIBHU KUMAR SINGH
  //   19BCE0215
endmodule
