// Logisim project BinaryCounterUsingSR.circ as structural Verilog: 1 circuit, main circuit main
module main (
  input  in_1
);

  wire clock_1_out, not_1_out, not_2_out, not_3_out, s_r_ff_1_q, s_r_ff_2_q, s_r_ff_3_q;

  not not_1 (not_1_out, s_r_ff_2_q);
  not not_2 (not_2_out, s_r_ff_3_q);
  not not_3 (not_3_out, s_r_ff_1_q);
  Clock clock_1 (.out(clock_1_out));
  S_R_Flip_Flop s_r_ff_1 (
    .S(s_r_ff_2_q), .clk(clock_1_out), .R(not_1_out), .Q(s_r_ff_1_q), .en(in_1));  // open: Qn, preset, reset
  S_R_Flip_Flop s_r_ff_2 (
    .S(s_r_ff_3_q), .clk(clock_1_out), .R(not_2_out), .Q(s_r_ff_2_q), .en(in_1));  // open: Qn, preset, reset
  S_R_Flip_Flop s_r_ff_3 (
    .S(not_3_out), .clk(clock_1_out), .R(s_r_ff_1_q), .Q(s_r_ff_3_q), .en(in_1));  // open: Qn, preset, reset

  // Notes on the sheet:
  //   VIBHU KUMAR SINGH
  //   19BCE0215
  //   A
  //   B
  //   C
endmodule
