// Logisim project DFlipFlop.circ as structural Verilog: 1 circuit, main circuit main
module main (
  input  D,
  input  in_2,
  input  in_3,
  input  in_4,
  output Q_t_1
);

  wire clock_1_out;

  Clock clock_1 (.out(clock_1_out));
  D_Flip_Flop d_ff_1 (.clk(clock_1_out), .D(D), .Q(Q_t_1), .preset(in_2), .en(in_3), .reset(in_4));  // open: Qn

  // Notes on the sheet:
  //   clk
  //   D Flip Flop
  //   VIBHU KUMAR SINGH
  //   19BCE0215
endmodule
