// Logisim project JKFlipFlop.circ as structural Verilog: 1 circuit, main circuit main
module main (
  input  J,
  input  K,
  input  in_3,
  input  in_4,
  input  in_5,
  output Q_t_1
);

  wire clock_1_out;

  Clock clock_1 (.out(clock_1_out));
  J_K_Flip_Flop j_k_ff_1 (
    .J(J), .clk(clock_1_out), .K(K), .Q(Q_t_1), .preset(in_3), .en(in_4), .reset(in_5));  // open: Qn

  // Notes on the sheet:
  //   clk
  //   JK Flip Flop
  //   VIBHU KUMAR SINGH
  //   19BCE0215
endmodule
