// Logisim project SRFlipFlop.circ as structural Verilog: 1 circuit, main circuit main
module main (
  input  S,
  input  R,
  input  in_3,
  input  in_4,
  input  in_5,
  output Q_t_1
);

  wire clock_1_out;

  Clock clock_1 (.out(clock_1_out));
  S_R_Flip_Flop s_r_ff_1 (
    .S(S), .clk(clock_1_out), .R(R), .Q(Q_t_1), .preset(in_3), .reset(in_5), .en(in_4));  // open: Qn

  // Notes on the sheet:
  //   clk
  //   S-R Flip Flop
  //   VIBHU KUMAR SINGH
  //   19BCE0215
endmodule
