// Logisim project StateDiagramDesign.circ as structural Verilog: 1 circuit, main circuit main
module main (
  input  X,
  input  in_2,
  output A,
  output B
);

  wire and_1_out, and_2_out, clock_1_out, not_1_out, xnor_1_out;

  not not_1 (not_1_out, X);
  xnor xnor_1 (xnor_1_out, A, X);
  and and_1 (and_1_out, B, not_1_out);
  and and_2 (and_2_out, B, X);
  Clock clock_1 (.out(clock_1_out));
  J_K_Flip_Flop j_k_ff_1 (
    .J(and_1_out), .clk(clock_1_out), .K(and_2_out), .Q(A), .en(in_2));  // open: Qn, preset, reset
  J_K_Flip_Flop j_k_ff_2 (.J(X), .clk(clock_1_out), .K(xnor_1_out), .Q(B), .en(in_2));  // open: Qn, preset, reset

  // Notes on the sheet:
  //   VIBHU KUMAR SINGH
  //   19BCE0215
  //   State Diagram Design
endmodule
