// Logisim project TFlipFlop.circ as structural Verilog: 1 circuit, main circuit main
module main (
  input  T,
  input  in_2,
  input  in_3,
  input  in_4,
  output Q_t_1
);

  wire clock_1_out;

  Clock clock_1 (.out(clock_1_out));
  T_Flip_Flop t_ff_1 (.clk(clock_1_out), .T(T), .Q(Q_t_1), .preset(in_2), .reset(in_4), .en(in_3));  // open: Qn

  // Notes on the sheet:
  //   clk
  //   T Flip Flop
  //   VIBHU KUMAR SINGH
  //   19BCE0215
endmodule
