// Logisim project UpDownBCDCounter.circ as structural Verilog: 1 circuit, main circuit main
module main (
  input  in_1,
  input  in_2,
  input  in_3,
  output out_4,
  output out_5,
  output out_6,
  output out_7
);

  wire and_1_out, and_2_out, and_3_out, clock_1_out, j_k_ff_2_qn, j_k_ff_3_qn, j_k_ff_4_qn,
       multiplexer_1_out, multiplexer_2_out, multiplexer_3_out;

  Clock clock_1 (.out(clock_1_out));
  and and_1 (and_1_out, multiplexer_1_out, and_2_out);
  Multiplexer multiplexer_1 (.in0(out_5), .in1(j_k_ff_2_qn), .out(multiplexer_1_out), .sel(in_3));  // open: en
  J_K_Flip_Flop j_k_ff_1 (
    .J(and_1_out), .clk(clock_1_out), .K(and_1_out), .Q(out_4), .en(in_2));  // open: Qn, preset, reset
  and and_2 (and_2_out, multiplexer_2_out, and_3_out);
  J_K_Flip_Flop j_k_ff_2 (
    .J(and_2_out), .clk(clock_1_out), .K(and_2_out), .Q(out_5), .Qn(j_k_ff_2_qn), .en(in_2));  // open: preset, reset
  Multiplexer multiplexer_2 (.in0(out_6), .in1(j_k_ff_3_qn), .out(multiplexer_2_out), .sel(in_3));  // open: en
  J_K_Flip_Flop j_k_ff_3 (
    .J(and_3_out), .clk(clock_1_out), .K(and_3_out), .Q(out_6), .Qn(j_k_ff_3_qn), .en(in_2));  // open: preset, reset
  and and_3 (and_3_out, in_1, multiplexer_3_out);
  J_K_Flip_Flop j_k_ff_4 (
    .J(in_1), .clk(clock_1_out), .K(in_1), .Q(out_7), .Qn(j_k_ff_4_qn), .en(in_2));  // open: preset, reset
  Multiplexer multiplexer_3 (.in0(out_7), .in1(j_k_ff_4_qn), .out(multiplexer_3_out), .sel(in_3));  // open: en

  // Notes on the sheet:
  //   VIBHU KUMAR SINGH
  //   19BCE0215
endmodule
