// Logisim project Midsem.circ as structural Verilog: 1 circuit, main circuit main
module main (
  input  A,
  input  B,
  input  C,
  output F
);

  wire nand_1_out, nand_2_out, nand_3_out, nand_4_out, nand_5_out, nand_6_out;

  nand nand_1 (nand_1_out, A, A);
  nand nand_2 (nand_2_out, B, B);
  nand nand_3 (nand_3_out, C, C);
  nand nand_4 (nand_4_out, nand_1_out, nand_2_out, C);
  nand nand_5 (nand_5_out, A, nand_2_out, nand_3_out);
  nand nand_6 (nand_6_out, nand_1_out, B, nand_3_out);
  nand nand_7 (F, nand_5_out, nand_4_out, nand_6_out);
endmodule
